// Logisim project Add1bit.circ as structural Verilog: 2 circuits, main circuit Add1bit
module Add1bit (
  input  A,
  input  B,
  input  C_in,
  output D,
  output C_out
);

  wire and_1_out, and_2_out, and_3_out, xor_1_out;

  xor xor_1 (xor_1_out, A, B);
  and and_1 (and_1_out, A, B);
  and and_2 (and_2_out, B, C_in);
  and and_3 (and_3_out, A, B);
  xor xor_2 (D, xor_1_out, C_in);
  or or_1 (C_out, and_1_out, and_3_out, and_2_out);

  // Notes on the sheet:
  //   B: initial=0x1
endmodule

module Add4bit (
  input  [3:0] C_in,
  input  [3:0] A,
  input  [3:0] B,
  output [3:0] out_4,
  output [3:0] out_5
);

  wire add1bit_1_c_out, add1bit_2_c_out, add1bit_3_c_out;

  Add1bit add1bit_1 (.A(A[0]), .B(B[0]), .C_in(C_in[0]), .D(out_4[0]), .C_out(add1bit_1_c_out));
  Add1bit add1bit_2 (.A(A[1]), .B(B[1]), .C_in(add1bit_1_c_out), .D(out_4[1]), .C_out(add1bit_2_c_out));
  Add1bit add1bit_3 (.A(A[2]), .B(B[2]), .C_in(add1bit_2_c_out), .D(out_4[2]), .C_out(add1bit_3_c_out));
  Add1bit add1bit_4 (.A(A[2]), .B(B[2]), .C_in(add1bit_2_c_out), .D(out_4[2]), .C_out(add1bit_3_c_out));
  Add1bit add1bit_5 (.A(A[3]), .B(B[3]), .C_in(add1bit_3_c_out), .D(out_4[3]), .C_out(out_5[0]));
  // Pins of 1 and 4 bits meet at C_in
  // Pins of 1 and 4 bits meet at out_5
endmodule
