// Logisim project nunes_vaca.circ as structural Verilog: 11 circuits, main circuit bin_lin_3a8_top
module bin_lin_3a8_top (
);

  wire dipswitch_1_sw1, dipswitch_1_sw2;
  wire [2:0] dipswitch_1_sw6;
  wire [7:0] bin_lin_3a8_1_lin_o;

  DipSwitch dipswitch_1 (
    .sw1(dipswitch_1_sw1), .sw2(dipswitch_1_sw2), .sw6(dipswitch_1_sw6[0]), .sw7(dipswitch_1_sw6[1]),
    .sw8(dipswitch_1_sw6[2]));  // open: sw3, sw4, sw5
  bin_lin_3a8 bin_lin_3a8_1 (
    .en_i(dipswitch_1_sw1), .sel_i(dipswitch_1_sw2), .bin_i(dipswitch_1_sw6), .lin_o(bin_lin_3a8_1_lin_o));
  // NoConnect on nothing
  // PortIO #(.number(25)) portio_1: pin names not known; wires that end beside it: 1'b1, {{17{1'b0}}, bin_lin_3a8_1_lin_o}
endmodule

module bin_lin_3a8_sim (
  input  En,
  input  Sel,
  input  [2:0] Bin
);

  wire [7:0] bin_lin_3a8_1_lin_o;

  LED Lin7 (.in(bin_lin_3a8_1_lin_o[7]));
  LED Lin6 (.in(bin_lin_3a8_1_lin_o[6]));
  LED Lin5 (.in(bin_lin_3a8_1_lin_o[5]));
  LED Lin4 (.in(bin_lin_3a8_1_lin_o[4]));
  bin_lin_3a8 bin_lin_3a8_1 (.en_i(En), .sel_i(Sel), .bin_i(Bin), .lin_o(bin_lin_3a8_1_lin_o));
  LED Lin3 (.in(bin_lin_3a8_1_lin_o[3]));
  LED Lin2 (.in(bin_lin_3a8_1_lin_o[2]));
  LED Lin1 (.in(bin_lin_3a8_1_lin_o[1]));
  LED Lin0 (.in(bin_lin_3a8_1_lin_o[0]));
endmodule

module bin_lin_3a8 (
  input  en_i,
  input  sel_i,
  input  [2:0] bin_i,
  output [7:0] lin_o
);

  lin_o_0 lin_o_0_1 (.en_i(en_i), .sel_i(sel_i), .in_3(bin_i), .out_4(lin_o[0]));
  lin_o_1 lin_o_1_1 (.en_i(en_i), .sel_i(sel_i), .in_3(bin_i), .out_4(lin_o[1]));
  lin_o_2 lin_o_2_1 (.en_i(en_i), .sel_i(sel_i), .in_3(bin_i), .out_4(lin_o[2]));
  lin_o_3 lin_o_3_1 (.en_i(en_i), .sel_i(sel_i), .in_3(bin_i), .out_4(lin_o[3]));
  lin_o_4 lin_o_4_1 (.en_i(en_i), .sel_i(sel_i), .in_3(bin_i), .out_4(lin_o[4]));
  lin_o_5 lin_o_5_1 (.en_i(en_i), .sel_i(sel_i), .in_3(bin_i), .out_4(lin_o[5]));
  lin_o_6 lin_o_6_1 (.en_i(en_i), .sel_i(sel_i), .in_3(bin_i), .out_4(lin_o[6]));
  lin_o_7 lin_o_7_1 (.en_i(en_i), .sel_i(sel_i), .in_3(bin_i), .out_4(lin_o[7]));

  // Notes on the sheet:
  //   Ne pas modifier les entrées sorties !
endmodule

module lin_o_7 (
  input  en_i,
  input  sel_i,
  input  [2:0] in_3,
  output out_4
);

  wire and_1_out, and_2_out, not_1_out, not_2_out, not_3_out, not_4_out, or_1_out;

  not not_1 (not_1_out, in_3[0]);
  not not_2 (not_2_out, in_3[1]);
  not not_3 (not_3_out, in_3[2]);
  not not_4 (not_4_out, sel_i);
  and and_1 (and_1_out, sel_i, not_1_out, not_2_out, not_3_out);
  and and_2 (and_2_out, not_4_out, in_3[0], in_3[1], in_3[2]);
  or or_1 (or_1_out, and_1_out, and_2_out);
  and and_3 (out_4, en_i, or_1_out);
endmodule

module lin_o_6 (
  input  en_i,
  input  sel_i,
  input  [2:0] in_3,
  output out_4
);

  wire and_1_out, and_2_out, not_1_out, not_2_out, not_3_out, or_1_out;

  not not_1 (not_1_out, in_3[1]);
  not not_2 (not_2_out, in_3[2]);
  not not_3 (not_3_out, sel_i);
  and and_1 (and_1_out, sel_i, not_1_out, not_2_out);
  and and_2 (and_2_out, not_3_out, in_3[1], in_3[2]);
  or or_1 (or_1_out, and_1_out, and_2_out);
  and and_3 (out_4, en_i, or_1_out);
endmodule

module lin_o_5 (
  input  en_i,
  input  sel_i,
  input  [2:0] in_3,
  output out_4
);

  wire and_1_out, and_2_out, and_3_out, and_4_out, not_1_out, not_2_out, not_3_out, not_4_out, not_5_out,
       not_6_out, or_1_out;

  not not_1 (not_1_out, in_3[0]);
  not not_2 (not_2_out, in_3[2]);
  not not_3 (not_3_out, in_3[1]);
  not not_4 (not_4_out, in_3[2]);
  not not_5 (not_5_out, sel_i);
  not not_6 (not_6_out, sel_i);
  and and_1 (and_1_out, sel_i, not_1_out, not_2_out);
  and and_2 (and_2_out, sel_i, not_3_out, not_4_out);
  and and_3 (and_3_out, not_5_out, in_3[0], in_3[2]);
  and and_4 (and_4_out, not_6_out, in_3[1], in_3[2]);
  or or_1 (or_1_out, and_1_out, and_2_out, and_3_out, and_4_out);
  and and_5 (out_4, en_i, or_1_out);
endmodule

module lin_o_4 (
  input  en_i,
  input  sel_i,
  input  [2:0] in_3,
  output out_4
);

  wire and_1_out, and_2_out, not_1_out, not_2_out, or_1_out;

  not not_1 (not_1_out, in_3[2]);
  not not_2 (not_2_out, sel_i);
  and and_1 (and_1_out, sel_i, not_1_out);
  and and_2 (and_2_out, not_2_out, in_3[2]);
  or or_1 (or_1_out, and_1_out, and_2_out);
  and and_3 (out_4, en_i, or_1_out);
endmodule

module lin_o_3 (
  input  en_i,
  input  sel_i,
  input  [2:0] in_3,
  output out_4
);

  wire and_1_out, and_2_out, and_3_out, and_4_out, not_1_out, not_2_out, not_3_out, not_4_out, not_5_out,
       or_1_out;

  not not_1 (not_1_out, in_3[0]);
  not not_2 (not_2_out, in_3[1]);
  not not_3 (not_3_out, in_3[2]);
  not not_4 (not_4_out, sel_i);
  not not_5 (not_5_out, sel_i);
  and and_1 (and_1_out, sel_i, not_1_out, not_2_out);
  and and_2 (and_2_out, sel_i, not_3_out);
  and and_3 (and_3_out, not_4_out, in_3[2]);
  and and_4 (and_4_out, not_5_out, in_3[0], in_3[1]);
  or or_1 (or_1_out, and_1_out, and_2_out, and_3_out, and_4_out);
  and and_5 (out_4, en_i, or_1_out);
endmodule

module lin_o_2 (
  input  en_i,
  input  sel_i,
  input  [2:0] in_3,
  output out_4
);

  wire and_1_out, and_2_out, and_3_out, not_1_out, not_2_out, not_3_out, or_1_out;

  not not_1 (not_1_out, in_3[2]);
  not not_2 (not_2_out, in_3[1]);
  not not_3 (not_3_out, sel_i);
  and and_1 (and_1_out, sel_i, not_1_out);
  and and_2 (and_2_out, not_2_out, in_3[2]);
  and and_3 (and_3_out, not_3_out, in_3[1]);
  or or_1 (or_1_out, and_1_out, and_2_out, and_3_out);
  and and_4 (out_4, en_i, or_1_out);
endmodule

module lin_o_1 (
  input  en_i,
  input  sel_i,
  input  [2:0] in_3,
  output out_4
);

  wire and_1_out, and_2_out, and_3_out, and_4_out, and_5_out, not_1_out, not_2_out, not_3_out, not_4_out,
       not_5_out, or_1_out;

  not not_1 (not_1_out, in_3[1]);
  not not_2 (not_2_out, in_3[2]);
  not not_3 (not_3_out, in_3[0]);
  not not_4 (not_4_out, in_3[1]);
  not not_5 (not_5_out, sel_i);
  and and_1 (and_1_out, sel_i, not_1_out);
  and and_2 (and_2_out, in_3[1], not_2_out);
  and and_3 (and_3_out, not_3_out, in_3[1]);
  and and_4 (and_4_out, in_3[0], not_4_out);
  and and_5 (and_5_out, not_5_out, in_3[2]);
  or or_1 (or_1_out, and_1_out, and_2_out, and_3_out, and_4_out, and_5_out);
  and and_6 (out_4, en_i, or_1_out);
endmodule

module lin_o_0 (
  input  en_i,
  input  sel_i,
  input  [2:0] in_3,
  output out_4
);


  assign out_4 = en_i;
endmodule
