// Logisim project labo_alu_comp.circ as structural Verilog: 11 circuits, main circuit Add1bit
module Add1bit (
  input  c_i,
  input  a_i,
  input  b_i,
  output r_o,
  output c_o
);
endmodule

module Add4bits (
  input  c_i,
  input  [3:0] a_i,
  input  [3:0] b_i,
  output [3:0] r_o,
  output c_o
);
endmodule

module AddSub (
  input  op_i,
  input  [3:0] a_i,
  input  [3:0] b_i,
  output [3:0] r_o,
  output carry_o
);


  // Notes on the sheet:
  //   A vous de régler le nombre de bits pour l'opcode (supprimez ensuite ce texte)
endmodule

module Calculation (
  input  op_i,
  input  [3:0] a_i,
  input  [3:0] b_i,
  output [3:0] r_o,
  output zero_o,
  output carry_o,
  output negative_o,
  output overflow_o
);


  // Notes on the sheet:
  //   A vous de régler le nombre de bits pour l'opcode (supprimez ensuite ce texte)
endmodule

module Comp (
  input  negative_i,
  input  overflow_i,
  input  zero_i,
  input  carry_i,
  input  op_i,
  input  [3:0] a_i,
  input  [3:0] b_i,
  output cmp_o
);


  // Notes on the sheet:
  //   A vous de régler le nombre de bits pour l'opcode (supprimez ensuite ce texte)
endmodule

module Arithmetic_selection (
  input  op_i,
  input  [3:0] calculation_i,
  input  comp_i,
  output [3:0] arith_sel_o
);


  // Notes on the sheet:
  //   A vous de régler le nombre de bits pour l'opcode (supprimez ensuite ce texte)
endmodule

module Arithmetic (
  input  op_i,
  input  [3:0] a_i,
  input  [3:0] b_i,
  output carry_o,
  output overflow_o,
  output [3:0] arith_o
);


  // Notes on the sheet:
  //   A vous de régler le nombre de bits pour l'opcode (supprimez ensuite ce texte)
endmodule

module Logic (
  input  op_i,
  input  [3:0] a_i,
  input  [3:0] b_i,
  output [3:0] f_o
);


  // Notes on the sheet:
  //   A vous de régler le nombre de bits pour l'opcode (supprimez ensuite ce texte)
  //   NE PAS MODIFIER L'ORDRE DES ENTREES
endmodule

module OutputHandling (
  output [3:0] c_o,
  output error_o
);
endmodule

module ALU (
  input  [5:0] op_i,
  input  [3:0] a_i,
  input  [3:0] b_i,
  output [3:0] c_o,
  output error_o
);


  // Notes on the sheet:
  //   NE PAS MODIFIER L'ORDRE DES ENTREES
endmodule

module ALU_top (
  input  [5:0] op_i,
  input  [3:0] a,
  input  [3:0] b,
  output [3:0] c_o,
  output error_o
);

  ALU ALU_1 (.op_i(op_i), .a_i(a), .b_i(b), .c_o(c_o), .error_o(error_o));

  // Notes on the sheet:
  //   NE PAS MODIFIER !!!!
endmodule
